# Fritzing sketch Circuit Diagram (saved by Fritzing 0.8.7b)
# 18650 Li-ion Battery: CC-BY Dr Kristofer Chan, King's College London/Remote-research.org

parts:
  M1 = DOIT Esp32 DevKit v1 (30 pins long, 11 pins width) [part_number=ESP32S-PIN30]
  LoRa_Module1 = Ra-01 - LoRa Module SX1278 [part_number=SX1278]
  OLED1 = OLED 128x64 I2C Monochrome Display
  J1 = Piezo Speaker
  Q1 = TRANSISTOR_NPN [package=to-92-ammo]
  S1 = Pushbutton [package=THT]
  S2 = Pushbutton [package=THT]
  U1 = LM2596 step down module
  BAT1 = 18650 Li-ion Battery [package=battery-18650]
  BAT2 = 18650 Li-ion Battery [package=battery-18650]
  S3 = SPST Switch [package=r_sw_th]
  R1 = Resistor [tolerance=±5% resistance=10k package=THT]
  R2 = Resistor [tolerance=±5% resistance=4.7k package=THT]

nets:
  3V3: M1.3V3, LoRa_Module1.3.3V, OLED1.VDD
  GND: M1.GND, LoRa_Module1.GND, OLED1.GND, Q1.C, S1.leg0, S2.leg0, U1.IN-, U1.OUT-, BAT1.-
  N1: M1.D4, LoRa_Module1.DIO0
  N2: M1.RX2, LoRa_Module1.RESET
  N3: M1.D5, LoRa_Module1.NSS
  N4: M1.D18, LoRa_Module1.SCK
  N5: M1.D19, LoRa_Module1.MISO
  N6: M1.D21, OLED1.SDA
  N7: M1.D22, OLED1.SCK
  N8: M1.D23, LoRa_Module1.MOSI
  N9: M1.D32, Q1.B
  N10: M1.D33, R2.Pin_0
  N11: M1.D25, S2.leg1
  N12: M1.D26, S1.leg1
  N13: M1.VIN, J1.pin2, U1.OUT+
  N14: J1.pin1, Q1.E
  N15: U1.IN+, S3.S, R1.Pin_1
  N16: BAT1.+, BAT2.-
  N17: BAT2.+, S3.P

custom parts:
  DOIT Esp32 DevKit v1 (30 pins long, 11 pins width): The DOIT Esp32 DevKit v1 is one of the development board created by DOIT to evaluate the ESP-WROOM-32 module. It is based on the ESP32 microcontroller that boasts Wifi, Bluetooth, Ethernet and Low Power support all in a single chip. (vanepp) made breadboard work, adjusted pin numbering and labels and reduced size of schematic and cleaned up pcb. This chip is 30pins long (2 x15) and 11 pins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
  Ra-01 - LoRa Module SX1278: The Ra-01 LoRa Module featuring the SX1278 engine by Semtech. Module by AI-Thinker. Module (Ra-01) specifications from: https://www.banggood.com/Ra-01-Smart-Electronics-SX1278-LoRa-Spread-Spectrum-Wireless-Module-Ultra-Far-10KM-433M-p-1130769.html Description: Power supply: DC1.8-3.7V(3.3V) Chip: SX1278 Frequency: 433Mhz Operating temperature: -40~+85°C On Sheild Description (may vary by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
  LM2596 step down module: LM2596 DC-DC step down power supply module 3 A.
  18650 Li-ion Battery: 18650 li-ion Battery Standard 18650 battery with interactive connectors Creative Common Attribution 4.0 International (CC-BY 4.0) license. Any use of this part requires attribution of Dr Kristofer Chan, Department of Geography, King's College London. Contact kristofer.chan [at] kcl.ac.uk OR kris [at] remote-research.org for further information.
